# Fritzing sketch cansat wiring (saved by Fritzing 0.9.3b)
circuit board: 8.86179cm x 2.96615cm
breadboards: 1

parts:
  Part1 = Arduino Nano (Rev3.0)
  Part3 = Adafruit Ultimate GPS v3 [part_number="Adafruit #746"]
  U1 = Voltage Regulator - 3.3V [package="TO220 [THT]"]
  power = Header 2 [package=jst-2-pth-ns]
  Part2 = Adafruit BME680
  HC-1 = HC-12 Module
  C1 = Capacitor Polarized [package=cpol-radial-10uf-25v]

nets:
  GND: Part1.GND, Part3.GND, U1.GND, power.1, Part2.GND, HC-1.GND, C1.-
  N1: Part1.D2, Part3.RX
  N2: Part1.D3, Part3.TX
  N3: Part1.D4, HC-1.RXD
  N4: Part1.D5, HC-1.TXD
  VIN: Part1.VIN, Part3.VIN, U1.output_voltage, Part2.VIN, HC-1.VCC, C1.+
  N5: Part1.A5, Part2.SCK/SCL
  N6: Part1.A4, Part2.SDI/SDA
  N7: U1.input_voltage, power.2

custom parts:
  Adafruit Ultimate GPS v3: We carry a few different GPS modules here in the Adafruit shop, but none that satisfied our every desire - that's why we designed this little GPS breakout board. We believe this is the Ultimate GPS module, so we named it that. It's got everything you want and more: -165 dBm sensitivity, 10 Hz updates, 66 channels 5V friendly design and only 20mA current draw Breadboard friendly + two mounting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
  HC-12 Module: HC-12 433Mhz Module
